// Logisim project s-mips.circ as structural Verilog: 14 circuits, main circuit S-MIPS Board
module S_MIPS_Board (
  input  DESHABILITAR_DISPATCHER,
  output halt
);

  wire button_1_out, CLK, CS, d_ff_1_q, LCLR, LoadRAM, LoadRAMOn, LW, R_R_W, R_W, ram_dispatcher_1_finished,
       RCS, Reset_out, RST, TTY_EN;
  wire [2:0] KDB;
  wire [3:0] LMask, Mask, ram_1_read_time, ram_1_write_time, RMask;
  wire [6:0] KDB_DATA, TTY_DATA;
  wire [15:0] Addr, LAddr, RAddr;
  wire [31:0] I0, I1, I2, I3, LData, ram_1_data_out_0, ram_1_data_out_1, ram_1_data_out_2, ram_1_data_out_3,
       RI0, RI1, RI2, RI3;

  TTY #(.rows(25), .cols(80)) tty_1 (.data(TTY_DATA), .clk(CLK), .we(TTY_EN), .clr(RST));
  not not_1 (LoadRAMOn, ram_dispatcher_1_finished);
  RAM_Dispatcher ram_dispatcher_1 (
    .WriteTime(ram_1_write_time), .Clock(CLK), .Data(LData), .Address(LAddr), .Mask(LMask),
    .Finished(ram_dispatcher_1_finished), .Write(LW), .CLR(LCLR));
  Keyboard #(.buflen(64)) keyboard_1 (.clk(CLK), .re(KDB[0]), .avail(KDB[2]), .data(KDB_DATA));  // open: clr
  RAM ram_1 (
    .Address(RAddr), .Data_Out_0(ram_1_data_out_0), .Data_Out_1(ram_1_data_out_1),
    .Data_Out_2(ram_1_data_out_2), .Data_Out_3(ram_1_data_out_3), .Data_In_0(RI0), .Data_In_1(RI1),
    .Data_In_2(RI2), .Data_In_3(RI3), .Mask(RMask), .nRead_Write(R_R_W), .Chip_Select(RCS),
    .Read_Time(ram_1_read_time), .Reset(button_1_out), .Write_Time(ram_1_write_time));
  Button button_1 (.out(button_1_out));
  D_Flip_Flop d_ff_1 (.clk(CLK), .D(1'b1), .Q(d_ff_1_q), .reset(Reset_out));  // open: Qn, preset, en
  Button Reset (.out(Reset_out));
  S_MIPS s_mips_1 (
    .Kbd_Enable(KDB[0]), .Address(Addr), .Kbd_Clear(KDB[1]), .Kbd_Available(KDB[2]), .RAM_In_0(I0),
    .Kbd_ASCII_Data(KDB_DATA), .RAM_In_1(I1), .TTY_Enable(TTY_EN), .RAM_In_2(I2), .RAM_In_3(I3),
    .TTY_ASCII_Data(TTY_DATA), .Reset(RST), .RAM_Out_0(ram_1_data_out_0), .Clock(CLK),
    .RAM_Out_1(ram_1_data_out_1), .Stop(halt), .RAM_Out_2(ram_1_data_out_2), .RAM_Out_3(ram_1_data_out_3),
    .Mask(Mask), .Read_Time(ram_1_read_time), .Write_Time(ram_1_write_time), .nRead_Write(R_W),
    .Chip_Select(CS));
  D_Flip_Flop d_ff_2 (.clk(CLK), .D(d_ff_1_q), .Qn(LCLR), .reset(Reset_out));  // open: Q, preset, en
  or or_1 (RST, LCLR, LoadRAM);
  Clock clock_1 (.out(CLK));
  Multiplexer #(.width(32), .enable("false")) multiplexer_1 (.in0(I0), .in1(LData), .out(RI0), .sel(LoadRAM));
  Multiplexer #(.width(32), .enable("false")) multiplexer_2 (.in0(I1), .in1(LData), .out(RI1), .sel(LoadRAM));
  Multiplexer #(.width(32), .enable("false")) multiplexer_3 (.in0(I2), .in1(LData), .out(RI2), .sel(LoadRAM));
  Multiplexer #(.width(32), .enable("false")) multiplexer_4 (.in0(I3), .in1(LData), .out(RI3), .sel(LoadRAM));
  and and_1 (LoadRAM, ~DESHABILITAR_DISPATCHER, LoadRAMOn);  // AND_Gate
  Multiplexer #(.width(16), .enable("false")) multiplexer_5 (.in0(Addr), .in1(LAddr), .out(RAddr), .sel(LoadRAM));
  Multiplexer #(.width(4), .enable("false")) multiplexer_6 (.in0(Mask), .in1(LMask), .out(RMask), .sel(LoadRAM));
  Multiplexer #(.enable("false")) multiplexer_7 (.in0(CS), .in1(LW), .out(RCS), .sel(LoadRAM));
  Multiplexer #(.enable("false")) multiplexer_8 (.in0(R_W), .in1(LW), .out(R_R_W), .sel(LoadRAM));

  // Notes on the sheet:
  //   NO MODIFICAR
  //   Keyboard
endmodule

module RAM (
  input  [15:0] Address,
  input  [31:0] Data_In_0,
  input  [31:0] Data_In_1,
  input  [31:0] Data_In_2,
  input  [31:0] Data_In_3,
  input  [3:0] Mask,
  input  nRead_Write,
  input  Chip_Select,
  input  Reset,
  output [31:0] Data_Out_0,
  output [31:0] Data_Out_1,
  output [31:0] Data_Out_2,
  output [31:0] Data_Out_3,
  output [3:0] Read_Time,
  output [3:0] Write_Time
);

  wire and_2_out, and_3_out, and_4_out, and_5_out, and_6_out, and_7_out, and_8_out, and_9_out, Changed, CLK,
       comparator_2_eq, comparator_3_eq, comparator_4_eq, comparator_5_eq, comparator_6_eq, Count,
       demultiplexer_3_out0, Idle, Idle_q, Load, Load0, Load1, nand_1_out, or_1_out, or_2_out, or_3_out,
       or_4_out, or_5_out, or_6_out, or_7_out, or_8_out, or_9_out, or_10_out, Proc_q, Update_Mem, Zero_Time;
  wire [3:0] counter_1_q, multiplexer_1_out, subtractor_1_out;
  wire [31:0] register_1_q, register_2_q, register_3_q, register_4_q, register_5_q;

  // Probe on 4'b0011
  // Probe on 4'b0010
  Multiplexer #(.width(4), .enable("false")) multiplexer_1 (
    .in0(4'b0011), .in1(4'b0010), .out(multiplexer_1_out), .sel(nRead_Write));
  or or_1 (or_1_out, Idle, Update_Mem);
  or or_2 (or_2_out, ~Chip_Select, Reset);  // OR_Gate
  Subtractor #(.width(4)) subtractor_1 (.a(multiplexer_1_out), .b(4'b0010), .out(subtractor_1_out));  // open: bin, bout
  Demultiplexer #(.enable("false")) demultiplexer_1 (.out0(Idle), .out1(Load0), .in(Idle_q), .sel(Changed));
  D_Flip_Flop u_Idle (.clk(CLK), .D(or_1_out), .Q(Idle_q), .preset(or_2_out));  // open: Qn, en, reset
  // Probe on counter_1_q
  Counter #(.width(4), .max('hf)) counter_1 (
    .load(Load), .D(subtractor_1_out), .count(Count), .Q(counter_1_q), .clk(CLK), .clr(or_3_out));  // open: carry
  or or_3 (or_3_out, ~Chip_Select, Reset);  // OR_Gate
  Comparator #(.width(4), .mode("unsigned")) comparator_1 (
    .a(4'b0000), .b(counter_1_q), .eq(Zero_Time));  // open: gt, lt
  or or_4 (or_4_out, Count, Load0, Load1);
  Register #(.width(32)) register_1 (.D(Data_In_0), .en(Chip_Select), .Q(register_1_q), .clk(CLK), .clr(or_5_out));
  or or_5 (or_5_out, ~Chip_Select, Reset);  // OR_Gate
  Register #(.width(32)) register_2 (.D(Data_In_1), .en(Chip_Select), .Q(register_2_q), .clk(CLK), .clr(or_6_out));
  or or_6 (or_6_out, ~Chip_Select, Reset);  // OR_Gate
  Register #(.width(32)) register_3 (.D(Data_In_2), .en(Chip_Select), .Q(register_3_q), .clk(CLK), .clr(or_7_out));
  or or_7 (or_7_out, ~Chip_Select, Reset);  // OR_Gate
  Register #(.width(32)) register_4 (.D(Data_In_3), .en(Chip_Select), .Q(register_4_q), .clk(CLK), .clr(or_8_out));
  or or_8 (or_8_out, ~Chip_Select, Reset);  // OR_Gate
  Register #(.width(32)) register_5 (
    .D({{11{1'b1}}, nRead_Write, Mask, Address}), .en(Chip_Select), .Q(register_5_q), .clk(CLK),
    .clr(or_9_out));
  or or_9 (or_9_out, ~Chip_Select, Reset);  // OR_Gate
  D_Flip_Flop Proc (.clk(CLK), .D(or_4_out), .Q(Proc_q), .reset(or_10_out));  // open: Qn, preset, en
  or or_10 (or_10_out, ~Chip_Select, Reset);  // OR_Gate
  Demultiplexer #(.enable("false")) demultiplexer_2 (
    .out0(Count), .out1(Update_Mem), .in(demultiplexer_3_out0), .sel(Zero_Time));
  Demultiplexer #(.enable("false")) demultiplexer_3 (
    .out0(demultiplexer_3_out0), .out1(Load1), .in(Proc_q), .sel(Changed));
  Clock clock_1 (.out(CLK));
  Comparator #(.width(32)) comparator_2 (.a(register_1_q), .b(Data_In_0), .eq(comparator_2_eq));  // open: gt, lt
  Comparator #(.width(32)) comparator_3 (.a(register_2_q), .b(Data_In_1), .eq(comparator_3_eq));  // open: gt, lt
  Comparator #(.width(32)) comparator_4 (.a(register_3_q), .b(Data_In_2), .eq(comparator_4_eq));  // open: gt, lt
  Comparator #(.width(32)) comparator_5 (.a(register_4_q), .b(Data_In_3), .eq(comparator_5_eq));  // open: gt, lt
  Comparator #(.width(32)) comparator_6 (
    .a(register_5_q), .b({{11{1'b1}}, nRead_Write, Mask, Address}), .eq(comparator_6_eq));  // open: gt, lt
  nand nand_1 (nand_1_out, comparator_6_eq, comparator_2_eq, comparator_3_eq, comparator_4_eq, comparator_5_eq);
  and and_1 (Changed, nand_1_out, Chip_Select);
  or or_11 (Load, Count, Load1, Load0);
  and and_2 (and_2_out, Mask[0], Update_Mem, nRead_Write);
  and and_3 (and_3_out, Mask[1], Update_Mem, nRead_Write);
  and and_4 (and_4_out, Mask[2], Update_Mem, nRead_Write);
  and and_5 (and_5_out, Mask[3], Update_Mem, nRead_Write);
  RAM_part #(.addrWidth(16), .dataWidth(32), .bus("separate")) ram_1 (
    .addr(Address), .din(Data_In_0), .data(Data_Out_0), .str(and_2_out), .sel(Chip_Select), .clk(CLK),
    .ld(and_6_out), .clr(Reset));
  and and_6 (and_6_out, ~nRead_Write, Idle);  // AND_Gate
  RAM_part #(.addrWidth(16), .dataWidth(32), .bus("separate")) ram_2 (
    .addr(Address), .din(Data_In_1), .data(Data_Out_1), .str(and_3_out), .sel(Chip_Select), .clk(CLK),
    .ld(and_7_out), .clr(Reset));
  and and_7 (and_7_out, ~nRead_Write, Idle);  // AND_Gate
  RAM_part #(.addrWidth(16), .dataWidth(32), .bus("separate")) ram_3 (
    .addr(Address), .din(Data_In_2), .data(Data_Out_2), .str(and_4_out), .sel(Chip_Select), .clk(CLK),
    .ld(and_8_out), .clr(Reset));
  and and_8 (and_8_out, ~nRead_Write, Idle);  // AND_Gate
  RAM_part #(.addrWidth(16), .dataWidth(32), .bus("separate")) ram_4 (
    .addr(Address), .din(Data_In_3), .data(Data_Out_3), .str(and_5_out), .sel(Chip_Select), .clk(CLK),
    .ld(and_9_out), .clr(Reset));
  and and_9 (and_9_out, ~nRead_Write, Idle);  // AND_Gate

  assign Read_Time = 4'b0011;
  assign Write_Time = 4'b0010;

  // Other names for the same wires on the sheet: M0 = Mask[0]; M1 = Mask[1]; M2 = Mask[2]; M3 = Mask[3];
  //   RW = nRead_Write; CLR = Reset; CS = Chip_Select; Load2 = Count

  // Notes on the sheet:
  //   NO MODIFICAR
  //   excepto quizás los valores RT y WT
  //   BANK0
  //   BANK1
  //   BANK2
  //   BANK3
endmodule

module S_MIPS (
  input  Kbd_Available,
  input  [6:0] Kbd_ASCII_Data,
  input  [31:0] RAM_Out_0,
  input  [31:0] RAM_Out_1,
  input  Reset,
  input  [31:0] RAM_Out_2,
  input  Clock,
  input  [31:0] RAM_Out_3,
  input  [3:0] Read_Time,
  input  [3:0] Write_Time,
  output Kbd_Enable,
  output [15:0] Address,
  output Kbd_Clear,
  output TTY_Enable,
  output [6:0] TTY_ASCII_Data,
  output Stop,
  output [31:0] RAM_In_0,
  output [31:0] RAM_In_1,
  output [31:0] RAM_In_2,
  output [31:0] RAM_In_3,
  output [3:0] Mask,
  output nRead_Write,
  output Chip_Select
);


  // Other names for the same wires on the sheet: CLK = Clock; CLR = Reset; CS = Chip_Select;
  //   KBD_AVAIL = Kbd_Available; KBD_CLR = Kbd_Clear; KBD_DATA[6:0] = Kbd_ASCII_Data; RAM_A[15:0] = Address;
  //   RAM_INPUT_0[31:0] = RAM_In_0; RAM_INPUT_1[31:0] = RAM_In_1; RAM_INPUT_2[31:0] = RAM_In_2;
  //   RAM_INPUT_3[31:0] = RAM_In_3; RAM_MASK[3:0] = Mask; RAM_OUTPUT_0[31:0] = RAM_Out_0;
  //   RAM_OUTPUT_1[31:0] = RAM_Out_1; RAM_OUTPUT_2[31:0] = RAM_Out_2; RAM_OUTPUT_3[31:0] = RAM_Out_3;
  //   RW = nRead_Write; TTY_DATA[6:0] = TTY_ASCII_Data

  // Notes on the sheet:
  //   RAM ADDRESS
  //   DATA FROM RAM
  //   DATA TO RAM
  //   DATA WRITE MASK
  //   RAM TIMING
  //   RAM CONTROL
  //   KEYBOARD
  //   TTY
  //   SEQUENCING
endmodule

module RAM_Dispatcher (
  input  [3:0] WriteTime,
  input  Clock,
  input  CLR,
  output [31:0] Data,
  output [15:0] Address,
  output [3:0] Mask,
  output Finished,
  output Write
);

  wire demultiplexer_2_out1, demultiplexer_3_out1, End, IDLE_q, IncAddr, Load, or_1_out, or_2_out, While_q,
       WriteEnd;
  wire [3:0] counter_1_q;
  wire [31:0] CurrentAddress_q;

  Counter #(.width(32), .max('hffffffff)) CurrentAddress (
    .count(IncAddr), .Q({CurrentAddress_q[31:18], Address, CurrentAddress_q[1:0]}), .clk(Clock), .clr(CLR));  // open: load, D, carry
  or or_1 (or_1_out, IncAddr, demultiplexer_3_out1, Finished);
  D_Flip_Flop IDLE (.clk(Clock), .D(or_1_out), .Q(IDLE_q), .preset(CLR));  // open: Qn, en, reset
  Demultiplexer #(.enable("false")) demultiplexer_1 (.out0(Load), .out1(Finished), .in(IDLE_q), .sel(End));
  D_Flip_Flop While (.clk(Clock), .D(or_2_out), .Q(While_q), .reset(CLR));  // open: Qn, preset, en
  or or_2 (or_2_out, Write, Load);
  RAM_part #(.addrWidth(18), .dataWidth(32)) ram_1 (
    .addr({Address, CurrentAddress_q[1:0]}), .data(Data), .clk(Clock));  // open: sel, ld, clr
  Demultiplexer #(.enable("false")) demultiplexer_2 (
    .out0(Write), .out1(demultiplexer_2_out1), .in(While_q), .sel(WriteEnd));
  Decoder #(.select(2)) decoder_1 (
    .out0(Mask[0]), .out1(Mask[1]), .out2(Mask[2]), .out3(Mask[3]), .sel(CurrentAddress_q[1:0]));  // open: en
  Demultiplexer #(.enable("false")) demultiplexer_3 (
    .out0(IncAddr), .out1(demultiplexer_3_out1), .in(demultiplexer_2_out1), .sel(End));
  Counter #(.width(4), .max('hf)) counter_1 (
    .load(Load), .D(WriteTime), .count(Write), .Q(counter_1_q), .clk(Clock));  // open: carry, clr
  Comparator #(.width(32)) comparator_1 (.a(Data), .b({32{1'b1}}), .eq(End));  // open: gt, lt
  Comparator #(.width(4)) comparator_2 (.a(4'b0000), .b(counter_1_q), .eq(WriteEnd));  // open: gt, lt

  // Other names for the same wires on the sheet: CLK = Clock; Count = Write; WT[3:0] = WriteTime
endmodule

module ALU (
  input  [31:0] A,
  input  [31:0] B,
  input  [3:0] Selector,
  output [31:0] OUTPUT,
  output COUT,
  output N,
  output Z
);

  wire comparator_2_lt;
  wire [31:0] ADD, AND, DIV, DIVU, MULT, MULU, NOR, OR, SLT, SUB, XOR;

  Adder #(.width(32)) adder_1 (.a(A), .b(B), .out(ADD), .cout(COUT));  // open: cin
  Subtractor #(.width(32)) subtractor_1 (.a(A), .b(B), .out(SUB));  // open: bin, bout
  Multiplier #(.width(32)) multiplier_1 (.a(A), .b(B), .out(MULT));  // open: cin, cout
  Divider #(.width(32)) divider_1 (.a(A), .b(B), .out(DIV));  // open: upper, rem
  SMULT__SDIV smult_sdiv_1 (.A(A), .B(B), .MULU(MULT), .DIVU(DIV), .MULT(MULU), .DIV(DIVU));
  Multiplexer #(.select(4), .width(32), .enable("false")) multiplexer_1 (
    .in0(ADD), .in1(SUB), .in2(MULT), .in3(MULU), .in4(DIV), .in5(DIVU), .in6(AND), .in7(OR), .in8(NOR),
    .in9(XOR), .in10(SLT), .out(OUTPUT), .sel(Selector));  // open: in11, in12, in13, in14, in15
  assign OR = A | B;  // OR_Gate or_1, 32 bits wide
  assign XOR = A ^ B;  // XOR_Gate xor_1, 32 bits wide
  Comparator #(.width(32)) comparator_1 (.a(OUTPUT), .b({32{1'b0}}), .gt(N), .eq(Z));  // open: lt
  Comparator #(.width(32)) comparator_2 (.a(A), .b(B), .lt(comparator_2_lt));  // open: gt, eq
  assign AND = A & B;  // AND_Gate and_1, 32 bits wide
  assign NOR = ~(A | B);  // NOR_Gate nor_1, 32 bits wide
  assign SLT = {{31{1'b0}}, comparator_2_lt};  // Bit_Extender bit_extender_1

  // Other names for the same wires on the sheet: SELECT[3:0] = Selector
endmodule

module REGISTER_FILE (
  input  Read_Write,
  input  [4:0] DA,
  input  [31:0] DI,
  input  [4:0] SA,
  input  [4:0] SB,
  input  clk,
  input  reset,
  input  E_Push,
  input  E_Pop,
  input  E_Hi_Lo,
  input  [31:0] High,
  input  [31:0] Low,
  output [31:0] HI,
  output [31:0] Lo,
  output [31:0] A,
  output [31:0] B
);

  wire E0, E1, E2, E3, E4, E5, E6, E7, E8, E9, E10, E11, E12, E13, E14, E15, E16, E17, E18, E19, E20, E21,
       E22, E23, E24, E25, E26, E27, E28, E29, E30, E31;
  wire [31:0] Q0, Q1, Q2, Q3, Q4, Q5, Q6, Q7, Q8, Q9, Q10, Q11, Q12, Q13, Q14, Q15, Q16, Q17, Q18, Q19, Q20,
       Q21, Q22, Q23, Q24, Q25, Q26, Q27, Q28, Q29, Q30, Q31;

  Demultiplexer #(.select(5), .enable("false")) demultiplexer_1 (
    .out0(E0), .out1(E1), .out2(E2), .out3(E3), .out4(E4), .out5(E5), .out6(E6), .out7(E7), .out8(E8),
    .out9(E9), .out10(E10), .out11(E11), .out12(E12), .out13(E13), .out14(E14), .out15(E15), .out16(E16),
    .out17(E17), .out18(E18), .out19(E19), .out20(E20), .out21(E21), .out22(E22), .out23(E23), .out24(E24),
    .out25(E25), .out26(E26), .out27(E27), .out28(E28), .out29(E29), .out30(E30), .out31(E31),
    .in(Read_Write), .sel(DA));
  Register #(.width(32)) register_1 (.D({32{1'b0}}), .en(E0), .Q(Q0), .clk(clk), .clr(reset));
  Register #(.width(32)) register_2 (.D(DI), .en(E1), .Q(Q1), .clk(clk), .clr(reset));
  Register #(.width(32)) register_3 (.D(DI), .en(E2), .Q(Q2), .clk(clk), .clr(reset));
  Register #(.width(32)) register_4 (.D(DI), .en(E3), .Q(Q3), .clk(clk), .clr(reset));
  Register #(.width(32)) register_5 (.D(DI), .en(E4), .Q(Q4), .clk(clk), .clr(reset));
  Register #(.width(32)) register_6 (.D(DI), .en(E5), .Q(Q5), .clk(clk), .clr(reset));
  Register #(.width(32)) register_7 (.D(DI), .en(E6), .Q(Q6), .clk(clk), .clr(reset));
  Register #(.width(32)) register_8 (.D(DI), .en(E7), .Q(Q7), .clk(clk), .clr(reset));
  Register #(.width(32)) register_9 (.D(DI), .en(E8), .Q(Q8), .clk(clk), .clr(reset));
  Register #(.width(32)) register_10 (.D(DI), .en(E9), .Q(Q9), .clk(clk), .clr(reset));
  Register #(.width(32)) register_11 (.D(DI), .en(E10), .Q(Q10), .clk(clk), .clr(reset));
  Register #(.width(32)) register_12 (.D(DI), .en(E11), .Q(Q11), .clk(clk), .clr(reset));
  Register #(.width(32)) register_13 (.D(DI), .en(E12), .Q(Q12), .clk(clk), .clr(reset));
  Register #(.width(32)) register_14 (.D(DI), .en(E13), .Q(Q13), .clk(clk), .clr(reset));
  Register #(.width(32)) register_15 (.D(DI), .en(E14), .Q(Q14), .clk(clk), .clr(reset));
  Register #(.width(32)) register_16 (.D(DI), .en(E15), .Q(Q15), .clk(clk), .clr(reset));
  Register #(.width(32)) register_17 (.D(DI), .en(E16), .Q(Q16), .clk(clk), .clr(reset));
  Register #(.width(32)) register_18 (.D(DI), .en(E17), .Q(Q17), .clk(clk), .clr(reset));
  Register #(.width(32)) register_19 (.D(DI), .en(E18), .Q(Q18), .clk(clk), .clr(reset));
  Register #(.width(32)) register_20 (.D(DI), .en(E19), .Q(Q19), .clk(clk), .clr(reset));
  Register #(.width(32)) register_21 (.D(DI), .en(E20), .Q(Q20), .clk(clk), .clr(reset));
  Register #(.width(32)) register_22 (.D(DI), .en(E21), .Q(Q21), .clk(clk), .clr(reset));
  Register #(.width(32)) register_23 (.D(DI), .en(E22), .Q(Q22), .clk(clk), .clr(reset));
  Register #(.width(32)) register_24 (.D(DI), .en(E23), .Q(Q23), .clk(clk), .clr(reset));
  Register #(.width(32)) register_25 (.D(DI), .en(E24), .Q(Q24), .clk(clk), .clr(reset));
  Register #(.width(32)) register_26 (.D(DI), .en(E25), .Q(Q25), .clk(clk), .clr(reset));
  Register #(.width(32)) register_27 (.D(DI), .en(E26), .Q(Q26), .clk(clk), .clr(reset));
  Register #(.width(32)) register_28 (.D(DI), .en(E27), .Q(Q27), .clk(clk), .clr(reset));
  Register #(.width(32)) register_29 (.D(DI), .en(E28), .Q(Q28), .clk(clk), .clr(reset));
  Register #(.width(32)) register_30 (.D(DI), .en(E29), .Q(Q29), .clk(clk), .clr(reset));
  Register #(.width(32)) register_31 (.D(DI), .en(E30), .Q(Q30), .clk(clk), .clr(reset));
  Register #(.width(32)) register_32 (.D(DI), .en(E31), .Q(Q31), .clk(clk), .clr(reset));
  Register #(.width(32)) register_33 (.D(High), .en(E_Hi_Lo), .Q(HI), .clk(clk), .clr(reset));
  Register #(.width(32)) register_34 (.D(Low), .en(E_Hi_Lo), .Q(Lo), .clk(clk), .clr(reset));
  Multiplexer #(.select(5), .width(32), .enable("false")) multiplexer_1 (
    .in0(Q0), .in1(Q1), .in2(Q2), .in3(Q3), .in4(Q4), .in5(Q5), .in6(Q6), .in7(Q7), .in8(Q8), .in9(Q9),
    .in10(Q10), .in11(Q11), .in12(Q12), .in13(Q13), .in14(Q14), .in15(Q15), .in16(Q16), .in17(Q17),
    .in18(Q18), .in19(Q19), .in20(Q20), .in21(Q21), .in22(Q22), .in23(Q23), .in24(Q24), .in25(Q25),
    .in26(Q26), .in27(Q27), .in28(Q28), .in29(Q29), .in30(Q30), .in31(Q31), .out(A), .sel(SA));
  Multiplexer #(.select(5), .width(32), .enable("false")) multiplexer_2 (
    .in0(Q0), .in1(Q1), .in2(Q2), .in3(Q3), .in4(Q4), .in5(Q5), .in6(Q6), .in7(Q7), .in8(Q8), .in9(Q9),
    .in10(Q10), .in11(Q11), .in12(Q12), .in13(Q13), .in14(Q14), .in15(Q15), .in16(Q16), .in17(Q17),
    .in18(Q18), .in19(Q19), .in20(Q20), .in21(Q21), .in22(Q22), .in23(Q23), .in24(Q24), .in25(Q25),
    .in26(Q26), .in27(Q27), .in28(Q28), .in29(Q29), .in30(Q30), .in31(Q31), .out(B), .sel(SB));

  // Other names for the same wires on the sheet: RW = Read_Write

  // Notes on the sheet:
  //   INPUT
  //   OUTPUT
endmodule

module BRANCH_CONTROL (
  input  [25:0] DESTINO,
  input  [31:0] RS,
  input  [31:0] RT,
  input  [31:0] PC,
  input  [15:0] OFFSET,
  input  [1:0] BRANCH_SELECTOR
);

  wire [25:0] DEST;
  wire [31:0] PC_4, PC_4___4___OFFSET, PC_OUT;

  Multiplexer #(.select(2), .width(32), .enable("false")) multiplexer_1 (
    .in0(PC_4), .in1({PC[31:28], DEST, 2'b00}), .in2(PC_4___4___OFFSET), .in3(RS), .out(PC_OUT),
    .sel(BRANCH_SELECTOR));

  // Other names for the same wires on the sheet: P_C_____P_C31_____28______I25_____0_____0__2[31:2] = {PC[31:28], DEST};
  //   S[1:0] = BRANCH_SELECTOR
endmodule

module PROGRAM_COUNTER (
  input  [31:0] PC_IN,
  input  CLK,
  input  RESET,
  input  EN,
  output [31:0] PC_OUT
);

  Register #(.width(32)) register_1 (.D(PC_IN), .en(EN), .Q(PC_OUT), .clk(CLK), .clr(RESET));
endmodule

module INSTRUCTION_DECODER (
  input  [31:0] INSTRUCCION,
  input  [31:0] RS,
  input  [31:0] RT,
  output [4:0] RD,
  output [4:0] RT_2,
  output [4:0] RS_2,
  output [15:0] CONSTANTE,
  output [25:0] DESTINO_SALTO,
  output [1:0] BRANCH_SELECTOR,
  output HALT,
  output MFHI,
  output LW,
  output TTY,
  output MFLO,
  output SW,
  output RND,
  output POP,
  output KBD,
  output PUSH,
  output [3:0] ALU_SELECTOR
);

  wire _00_0000, _00_1010, _00_1100, _11_1000, _11_1111, ADD, ADDI, AND, and_25_out, and_26_out, and_27_out,
       and_28_out, and_29_out, ANDI, BEQ, BGTZ, BLEZ, BLTZ, BNE, comparator_1_eq, comparator_2_eq,
       comparator_3_eq, comparator_4_eq, comparator_5_eq, comparator_6_eq, comparator_7_eq, comparator_8_eq,
       comparator_9_eq, comparator_10_eq, comparator_11_eq, comparator_12_eq, comparator_13_eq,
       comparator_14_eq, comparator_15_eq, comparator_16_eq, comparator_17_eq, comparator_18_eq,
       comparator_27_eq, comparator_28_eq, comparator_35_eq, comparator_36_eq, comparator_37_eq,
       comparator_38_eq, comparator_39_eq, comparator_41_eq, DIV, DIVU, J, JR, MULT, MULU, NOP, NOR,
       nor_1_out, OR, or_1_out, or_2_out, or_3_out, or_4_out, or_5_out, or_7_out, or_8_out, ORI, RS_0, RS__0,
       RS__RT, SLT, SLTI, SLTIU, SLTU, SUB, XOR, XORI;
  wire [15:0] multiplier_1_out, OFFSET;
  wire [31:0] adder_2_out, bit_extender_1_out, PC, PC_4, Pc_4___4___OFFSET, Pc_4_t;

  and and_1 (NOR, _00_0000, comparator_1_eq);
  Comparator #(.width(6)) comparator_1 (.a(INSTRUCCION[5:0]), .b(6'b100111), .eq(comparator_1_eq));  // open: gt, lt
  and and_2 (XOR, _00_0000, comparator_2_eq);
  Comparator #(.width(6)) comparator_2 (.a(INSTRUCCION[5:0]), .b(6'b101000), .eq(comparator_2_eq));  // open: gt, lt
  Comparator #(.width(6)) comparator_3 (.a(INSTRUCCION[5:0]), .b(6'b101010), .eq(comparator_3_eq));  // open: gt, lt
  and and_3 (MFHI, _00_0000, comparator_4_eq);
  Comparator #(.width(6)) comparator_4 (.a(INSTRUCCION[5:0]), .b(6'b010000), .eq(comparator_4_eq));  // open: gt, lt
  Comparator #(.width(6)) comparator_5 (.a(INSTRUCCION[5:0]), .b(6'b010010), .eq(comparator_5_eq));  // open: gt, lt
  Comparator #(.width(6)) comparator_6 (.a(INSTRUCCION[5:0]), .b({6{1'b0}}), .eq(comparator_6_eq));  // open: gt, lt
  Comparator #(.width(6)) comparator_7 (.a(INSTRUCCION[5:0]), .b(6'b001000), .eq(comparator_7_eq));  // open: gt, lt
  Comparator #(.width(6)) comparator_8 (.a(INSTRUCCION[5:0]), .b(6'b011011), .eq(comparator_8_eq));  // open: gt, lt
  Comparator #(.width(6)) comparator_9 (.a(INSTRUCCION[5:0]), .b(6'b101011), .eq(comparator_9_eq));  // open: gt, lt
  or or_1 (or_1_out, ANDI, AND);
  or or_2 (or_2_out, ORI, OR);
  and and_4 (SLT, _00_0000, comparator_3_eq);
  and and_5 (MFLO, _00_0000, comparator_5_eq);
  and and_6 (NOP, _00_0000, comparator_6_eq);
  and and_7 (JR, _00_0000, comparator_7_eq);
  and and_8 (DIVU, _00_0000, comparator_8_eq);
  and and_9 (SLTU, _00_0000, comparator_9_eq);
  or or_3 (or_3_out, XOR, XORI);
  or or_4 (or_4_out, ADD, ADDI);
  or or_5 (or_5_out, SLT, SLTU, SLTI, SLTIU);
  Priority_Encoder #(.select(4)) priority_encoder_1 (
    .in0(or_4_out), .in1(SUB), .in2(MULT), .in3(MULU), .in4(DIV), .in5(DIVU), .in6(or_1_out), .in7(or_2_out),
    .in8(NOR), .in9(or_3_out), .in10(or_5_out), .out(ALU_SELECTOR));  // open: in11, in12, in13, in14, in15, gs, en_out, en_in
  and and_10 (ADD, _00_0000, comparator_10_eq);
  Comparator #(.width(6)) comparator_10 (.a(INSTRUCCION[5:0]), .b(6'b100000), .eq(comparator_10_eq));  // open: gt, lt
  and and_11 (SUB, _00_0000, comparator_11_eq);
  Comparator #(.width(6)) comparator_11 (.a(INSTRUCCION[5:0]), .b(6'b100010), .eq(comparator_11_eq));  // open: gt, lt
  and and_12 (MULT, _00_0000, comparator_12_eq);
  Comparator #(.width(6)) comparator_12 (.a(INSTRUCCION[5:0]), .b(6'b011000), .eq(comparator_12_eq));  // open: gt, lt
  Comparator #(.width(6)) comparator_13 (.a(INSTRUCCION[5:0]), .b(6'b011010), .eq(comparator_13_eq));  // open: gt, lt
  Comparator #(.width(6)) comparator_14 (.a(INSTRUCCION[5:0]), .b(6'b100100), .eq(comparator_14_eq));  // open: gt, lt
  Comparator #(.width(6)) comparator_15 (.a(INSTRUCCION[5:0]), .b(6'b100101), .eq(comparator_15_eq));  // open: gt, lt
  Comparator #(.width(6)) comparator_16 (.a(INSTRUCCION[5:0]), .b(6'b011001), .eq(comparator_16_eq));  // open: gt, lt
  Comparator #(.width(6)) comparator_17 (.a(INSTRUCCION[5:0]), .b({6{1'b0}}), .eq(comparator_17_eq));  // open: gt, lt
  Comparator #(.width(6)) comparator_18 (.a(INSTRUCCION[5:0]), .b(6'b000001), .eq(comparator_18_eq));  // open: gt, lt
  and and_13 (DIV, _00_0000, comparator_13_eq);
  and and_14 (AND, _00_0000, comparator_14_eq);
  and and_15 (OR, _00_0000, comparator_15_eq);
  and and_16 (MULU, _00_0000, comparator_16_eq);
  and and_17 (POP, _11_1000, comparator_17_eq);
  and and_18 (PUSH, _11_1000, comparator_18_eq);
  Comparator #(.width(6)) comparator_19 (.a(INSTRUCCION[31:26]), .b({6{1'b0}}), .eq(_00_0000));  // open: gt, lt
  Comparator #(.width(6)) comparator_20 (.a(INSTRUCCION[31:26]), .b({6{1'b1}}), .eq(_11_1111));  // open: gt, lt
  Comparator #(.width(6)) comparator_21 (.a(INSTRUCCION[31:26]), .b(6'b001010), .eq(_00_1010));  // open: gt, lt
  Comparator #(.width(6)) comparator_22 (.a(INSTRUCCION[31:26]), .b(6'b000100), .eq(BEQ));  // open: gt, lt
  Comparator #(.width(6)) comparator_23 (.a(INSTRUCCION[31:26]), .b(6'b001100), .eq(_00_1100));  // open: gt, lt
  Comparator #(.width(6)) comparator_24 (.a(INSTRUCCION[31:26]), .b(6'b000101), .eq(BNE));  // open: gt, lt
  Comparator #(.width(6)) comparator_25 (.a(INSTRUCCION[31:26]), .b(6'b000110), .eq(BLEZ));  // open: gt, lt
  Comparator #(.width(6)) comparator_26 (.a(INSTRUCCION[31:26]), .b(6'b001000), .eq(ADDI));  // open: gt, lt
  Comparator #(.width(6)) comparator_27 (.a(INSTRUCCION[5:0]), .b(6'b000010), .eq(comparator_27_eq));  // open: gt, lt
  Comparator #(.width(6)) comparator_28 (.a(INSTRUCCION[5:0]), .b(6'b000100), .eq(comparator_28_eq));  // open: gt, lt
  and and_19 (RND, _11_1111, comparator_27_eq);
  and and_20 (KBD, _11_1111, comparator_28_eq);
  Comparator #(.width(6)) comparator_29 (.a(INSTRUCCION[31:26]), .b(6'b100011), .eq(LW));  // open: gt, lt
  Comparator #(.width(6)) comparator_30 (.a(INSTRUCCION[31:26]), .b(6'b101011), .eq(SW));  // open: gt, lt
  Comparator #(.width(6)) comparator_31 (.a(INSTRUCCION[31:26]), .b(6'b111000), .eq(_11_1000));  // open: gt, lt
  Comparator #(.width(6)) comparator_32 (.a(INSTRUCCION[31:26]), .b(6'b000001), .eq(BLTZ));  // open: gt, lt
  Comparator #(.width(6)) comparator_33 (.a(INSTRUCCION[31:26]), .b(6'b000010), .eq(J));  // open: gt, lt
  Comparator #(.width(6)) comparator_34 (.a(INSTRUCCION[31:26]), .b(6'b000111), .eq(BGTZ));  // open: gt, lt
  Comparator #(.width(6)) comparator_35 (.a(INSTRUCCION[5:0]), .b(6'b000001), .eq(comparator_35_eq));  // open: gt, lt
  Comparator #(.width(6)) comparator_36 (.a(INSTRUCCION[5:0]), .b({6{1'b1}}), .eq(comparator_36_eq));  // open: gt, lt
  and and_21 (TTY, _11_1111, comparator_35_eq);
  and and_22 (HALT, comparator_36_eq, _11_1111);
  Comparator #(.width(6)) comparator_37 (.a(INSTRUCCION[5:0]), .b(6'b001101), .eq(comparator_37_eq));  // open: gt, lt
  Comparator #(.width(6)) comparator_38 (.a(INSTRUCCION[5:0]), .b(6'b001110), .eq(comparator_38_eq));  // open: gt, lt
  Comparator #(.width(32)) comparator_39 (.a(RS), .b({32{1'b0}}), .eq(comparator_39_eq), .lt(RS_0));  // open: gt
  Comparator #(.width(32)) comparator_40 (.a(RS), .b(RT), .eq(RS__RT));  // open: gt, lt
  and and_23 (ORI, _00_1100, comparator_37_eq);
  and and_24 (XORI, _00_1100, comparator_38_eq);
  and and_25 (and_25_out, BNE, ~RS__RT);  // AND_Gate
  and and_26 (and_26_out, BEQ, RS__RT);
  and and_27 (and_27_out, BLEZ, RS__0);
  and and_28 (and_28_out, BLTZ, RS_0);
  and and_29 (and_29_out, BGTZ, ~RS__0);  // AND_Gate
  and and_30 (ANDI, ~ORI, ~XORI, _00_1100);  // AND_Gate
  Comparator #(.width(6)) comparator_41 (.a(INSTRUCCION[5:0]), .b(6'b001011), .eq(comparator_41_eq));  // open: gt, lt
  or or_6 (RS__0, comparator_39_eq, RS_0);
  and and_31 (SLTIU, _00_1010, comparator_41_eq);
  and and_32 (SLTI, ~SLTIU, _00_1010);  // AND_Gate
  nor nor_1 (nor_1_out, and_25_out, and_26_out, and_27_out, and_28_out, and_29_out);
  or or_7 (or_7_out, and_25_out, and_26_out, and_27_out, and_28_out, and_29_out);
  or or_8 (or_8_out, NOP, nor_1_out);
  Priority_Encoder #(.select(2)) priority_encoder_2 (
    .in0(or_8_out), .in1(J), .in2(or_7_out), .in3(JR), .out(BRANCH_SELECTOR));  // open: gs, en_out, en_in
  Adder #(.width(32)) adder_1 (.a(PC), .b(32'h4), .out(Pc_4_t));  // open: cin, cout
  Adder #(.width(32)) adder_2 (.a(PC_4), .b(32'h4), .out(adder_2_out));  // open: cin, cout
  assign bit_extender_1_out = {{16{1'b0}}, multiplier_1_out};  // Bit_Extender bit_extender_1
  Multiplier #(.width(16)) multiplier_1 (.a(16'h4), .b(OFFSET), .out(multiplier_1_out));  // open: cin, cout
  Adder #(.width(32)) adder_3 (.a(adder_2_out), .b(bit_extender_1_out), .out(Pc_4___4___OFFSET));  // open: cin, cout

  assign CONSTANTE = INSTRUCCION[15:0];
  assign DESTINO_SALTO = INSTRUCCION[25:0];
  assign RD = INSTRUCCION[15:11];
  assign RS_2 = INSTRUCCION[25:21];
  assign RT_2 = INSTRUCCION[20:16];

  // Other names for the same wires on the sheet: FUNC_CODE[5:0] = INSTRUCCION[5:0]; I[31:0] = INSTRUCCION;
  //   OP_CODE[5:0] = INSTRUCCION[31:26]
endmodule

module R_RAM (
  input  [31:0] RAM_0,
  input  [31:0] RAM_1,
  input  [31:0] RAM_2,
  input  [31:0] RAM_3,
  input  [31:0] PC,
  output [31:0] Output
);

  Multiplexer #(.select(2), .width(32), .enable("false")) multiplexer_1 (
    .in0(RAM_0), .in1(RAM_1), .in2(RAM_2), .in3(RAM_3), .out(Output), .sel(PC[2:1]));

  // Other names for the same wires on the sheet: S[1:0] = PC[2:1]
endmodule

module W_RAM (
  input  [31:0] INPUT,
  input  [31:0] PC,
  output [3:0] MASK,
  output [31:0] RAM_0,
  output [31:0] RAM_1,
  output [31:0] RAM_2,
  output [15:0] ADDRESS,
  output [31:0] RAM_3
);

  Demultiplexer #(.select(2), .enable("false")) demultiplexer_1 (
    .out0(MASK[0]), .out1(MASK[1]), .out2(MASK[2]), .out3(MASK[3]), .in(1'b1), .sel(PC[3:2]));
  Demultiplexer #(.select(2), .width(32), .enable("false")) demultiplexer_2 (
    .out0(RAM_0), .out1(RAM_1), .out2(RAM_2), .out3(RAM_3), .in(INPUT), .sel(PC[3:2]));

  assign ADDRESS = PC[19:4];

  // Other names for the same wires on the sheet: S[1:0] = PC[3:2]
endmodule

module SMULT__SDIV (
  input  [31:0] A,
  input  [31:0] B,
  input  [31:0] MULU,
  input  [31:0] DIVU,
  output [31:0] MULT,
  output [31:0] DIV
);

  SIGN sign_1 (.SIGN_A(A[31]), .SIGN_B(B[31]), .S(DIV[31]));

  assign DIV[30:0] = DIVU[30:0];
  assign MULT = {DIV[31], MULU[30:0]};

  // Other names for the same wires on the sheet: SIGN = DIV[31]
endmodule

module SIGN (
  input  SIGN_A,
  input  SIGN_B,
  output S
);

  wire and_1_out, and_2_out, not_1_out, not_2_out;

  not not_1 (not_1_out, SIGN_A);
  not not_2 (not_2_out, SIGN_B);
  and and_1 (and_1_out, not_1_out, SIGN_B);
  and and_2 (and_2_out, SIGN_A, not_2_out);
  or or_1 (S, and_1_out, and_2_out);
endmodule

module DATA_PATH (
);

  wire clk;
  wire [1:0] BRANCH_SELECTOR;
  wire [3:0] ALU_SELECTOR;
  wire [4:0] RD, RS, RT;

  BRANCH_CONTROL branch_control_1 (.BRANCH_SELECTOR(BRANCH_SELECTOR));  // open: DESTINO, RS, RT, PC, OFFSET
  INSTRUCTION_DECODER instruction_decoder_1 (
    .RD(RD), .RT_2(RT), .ALU_SELECTOR(ALU_SELECTOR), .RS_2(RS), .BRANCH_SELECTOR(BRANCH_SELECTOR));  // open: INSTRUCCION, CONSTANTE, DESTINO_SALTO, LW, SW, POP, PUSH, MFHI, MFLO, HALT, TTY, RND, KBD, RS, RT
  REGISTER_FILE register_file_1 (.E_Pop(clk));  // open: Read_Write, DA, DI, SA, SB, clk, reset, A, B, E_Push, E_Hi_Lo, High, Low, HI, Lo
  ALU alu_1 (.Selector(ALU_SELECTOR));  // open: A, B, OUTPUT, COUT, N, Z
endmodule
